// Logisim project 1A.circ as structural Verilog: 1 circuit, main circuit main
module main (
  input  A,
  input  B,
  input  C,
  input  D,
  input  E,
  input  F,
  output Y
);

  wire AND_2_out, AND_out;

  and AND (AND_out, A, B, C);
  and AND_2 (AND_2_out, D, E);
  or u_Y (Y, AND_out, AND_2_out, F);

  // Notes on the sheet:
  //   21BCP359
endmodule
