// Logisim project 1B.circ as structural Verilog: 1 circuit, main circuit main
module main (
  input  A,
  input  B,
  output out_3
);

  wire A_prime_out, and_1_out, and_2_out, and_3_out, and_4_out, B_prime_out;

  not A_prime (A_prime_out, A);
  not B_prime (B_prime_out, B);
  and and_1 (and_1_out, A_prime_out, B_prime_out);
  and and_2 (and_2_out, A, B_prime_out);
  and and_3 (and_3_out, A_prime_out, B);
  and and_4 (and_4_out, A, B);
  or Z (out_3, and_1_out, and_2_out, and_3_out, and_4_out);

  // Notes on the sheet:
  //   21BCP359
endmodule
