// Logisim project 1C.circ as structural Verilog: 1 circuit, main circuit main
module main (
  input  A,
  input  B,
  output K
);

  wire not_1_out, not_2_out, or_1_out, or_2_out, or_3_out, or_4_out;

  not not_1 (not_1_out, A);
  not not_2 (not_2_out, B);
  or or_1 (or_1_out, not_1_out, not_2_out);
  or or_2 (or_2_out, A, not_2_out);
  or or_3 (or_3_out, not_1_out, B);
  or or_4 (or_4_out, A, B);
  and and_1 (K, or_1_out, or_2_out, or_3_out, or_4_out);

  // Notes on the sheet:
  //   21BCP359
endmodule
