// Logisim project 2A.circ as structural Verilog: 1 circuit, main circuit main
module main (
  input  A,
  input  B,
  input  C,
  input  D,
  input  E,
  output Y
);

  wire and_1_out, or_1_out, or_2_out;

  or or_1 (or_1_out, A, B);
  or or_2 (or_2_out, C, D, E);
  and and_1 (and_1_out, or_1_out, or_2_out);
  not not_1 (Y, and_1_out);

  // Notes on the sheet:
  //   21BCP359
endmodule
