// Logisim project 2B.circ as structural Verilog: 1 circuit, main circuit main
module main (
  input  A,
  input  B,
  output F
);

  wire and_1_out, and_2_out, not_1_out, not_2_out, not_3_out, not_4_out, or_1_out;

  not not_1 (not_1_out, A);
  not not_2 (not_2_out, B);
  and and_1 (and_1_out, A, not_2_out);
  and and_2 (and_2_out, not_1_out, not_2_out);
  not not_3 (not_3_out, and_1_out);
  not not_4 (not_4_out, and_2_out);
  or or_1 (or_1_out, not_3_out, not_4_out);
  not not_5 (F, or_1_out);

  // Notes on the sheet:
  //   21BCP359
endmodule
