// Logisim project 2C.circ as structural Verilog: 1 circuit, main circuit main
module main (
  input  A,
  input  in_2,
  output K
);

  wire and_1_out, not_1_out, not_2_out, not_3_out, not_4_out, or_1_out, or_2_out;

  not not_1 (not_1_out, A);
  not not_2 (not_2_out, in_2);
  or or_1 (or_1_out, not_1_out, not_2_out);
  or or_2 (or_2_out, in_2, not_2_out);
  not not_3 (not_3_out, or_1_out);
  not not_4 (not_4_out, or_2_out);
  and and_1 (and_1_out, not_3_out, not_4_out);
  not not_5 (K, and_1_out);

  // Notes on the sheet:
  //   21BCP359
endmodule
