// Logisim project 3A.circ as structural Verilog: 1 circuit, main circuit main
module main (
  input  A,
  input  B,
  output Y
);

  wire nand_1_out, nand_2_out, nand_3_out, nand_4_out;

  nand nand_1 (nand_1_out, A, A);
  nand nand_2 (nand_2_out, B, B);
  nand nand_3 (nand_3_out, A, nand_2_out);
  nand nand_4 (nand_4_out, B, nand_1_out);
  nand u_Y (Y, nand_3_out, nand_4_out);

  // Notes on the sheet:
  //   21BCP359
endmodule
