// Logisim project 3C.circ as structural Verilog: 1 circuit, main circuit main
module main (
  input  in_1,
  input  in_2,
  output Y
);

  wire nand_1_out;

  nand nand_1 (nand_1_out, in_1, in_2);
  nand nand_2 (Y, nand_1_out, nand_1_out);

  // Notes on the sheet:
  //   21BCP359
endmodule
