// Logisim project 3D.circ as structural Verilog: 1 circuit, main circuit main
module main (
  input  in_1,
  input  in_2,
  output Y
);

  wire nor_1_out;

  nor nor_1 (nor_1_out, in_1, in_2);
  nor nor_2 (Y, nor_1_out, nor_1_out);

  // Notes on the sheet:
  //   21BCP359
endmodule
