// Logisim project 3E.circ as structural Verilog: 1 circuit, main circuit main
module main (
  input  in_1,
  output Y
);

  nand nand_1 (Y, in_1, in_1);

  // Notes on the sheet:
  //   21BCP359
endmodule
