// Logisim project 3.circ as structural Verilog: 1 circuit, main circuit main
module main (
  input  A2,
  input  [1:0] A1_A0
);

  wire decoder_1_out0, decoder_1_out1, decoder_1_out2, decoder_1_out3, decoder_2_out0, decoder_2_out1,
       decoder_2_out2, decoder_2_out3, not_1_out;

  not not_1 (not_1_out, A2);
  Decoder #(.select(2)) decoder_1 (
    .out0(decoder_1_out0), .out1(decoder_1_out1), .out2(decoder_1_out2), .out3(decoder_1_out3), .sel(A1_A0),
    .en(not_1_out));
  Decoder #(.select(2)) decoder_2 (
    .out0(decoder_2_out0), .out1(decoder_2_out1), .out2(decoder_2_out2), .out3(decoder_2_out3), .sel(A1_A0),
    .en(A2));
  LED _0 (.in(decoder_1_out0));
  LED _1 (.in(decoder_1_out1));
  LED _2 (.in(decoder_1_out2));
  LED _3 (.in(decoder_1_out3));
  LED _4 (.in(decoder_2_out0));
  LED _5 (.in(decoder_2_out1));
  LED _6 (.in(decoder_2_out2));
  LED _7 (.in(decoder_2_out3));

  // Notes on the sheet:
  //   21BCP359
endmodule
