// Logisim project 5.circ as structural Verilog: 1 circuit, main circuit main
module main (
  input  I0,
  input  I1,
  input  I2,
  input  I3,
  input  [1:0] S0_S1,
  input  E
);

  wire multiplexer_1_out;

  Multiplexer #(.select(2)) multiplexer_1 (
    .in0(I0), .in1(I1), .in2(I2), .in3(I3), .out(multiplexer_1_out), .sel(S0_S1), .en(E));
  LED led_1 (.in(multiplexer_1_out));

  // Notes on the sheet:
  //   21BCP359
endmodule
