// Logisim project 1.circ as structural Verilog: 1 circuit, main circuit main
module main (
  input  S,
  input  R,
  output Q,
  output Q_prime
);

  wire not_1_out, not_2_out;

  not not_1 (not_1_out, S);
  not not_2 (not_2_out, R);
  nand nand_1 (Q, not_1_out, Q_prime);
  nand nand_2 (Q_prime, Q, not_2_out);

  // Notes on the sheet:
  //   21BCP359.
endmodule
