// Logisim project 9.2.circ as structural Verilog: 1 circuit, main circuit main
module main (
  input  J,
  input  Clk,
  input  J_2,
  output Q,
  output Q_prime
);

  wire nand_1_out, nand_2_out;

  nand nand_1 (nand_1_out, Q_prime, J, Clk);
  nand nand_2 (nand_2_out, Clk, J_2, Q);
  nand nand_3 (Q, nand_1_out, Q_prime);
  nand nand_4 (Q_prime, Q, nand_2_out);
endmodule
