// Logisim project 9.4.circ as structural Verilog: 1 circuit, main circuit main
module main (
  input  D,
  input  Clk,
  output Q,
  output Q_prime
);

  wire nand_1_out, nand_2_out, not_1_out;

  not not_1 (not_1_out, D);
  nand nand_1 (nand_1_out, Q_prime, D, Clk);
  nand nand_2 (nand_2_out, Clk, not_1_out, Q);
  nand nand_3 (Q, nand_1_out, Q_prime);
  nand nand_4 (Q_prime, Q, nand_2_out);

  // Notes on the sheet:
  //   21BCP359
endmodule
