// Logisim project 9.6.circ as structural Verilog: 1 circuit, main circuit main
module main (
  input  T,
  input  Clk,
  output Q,
  output Q_prime
);

  wire nand_1_out, nand_2_out;

  nand nand_1 (nand_1_out, Q_prime, T, Clk);
  nand nand_2 (nand_2_out, Clk, T, Q);
  nor nor_1 (Q, nand_1_out, Q_prime);
  nor nor_2 (Q_prime, Q, nand_2_out);

  // Notes on the sheet:
  //   21BCP359
endmodule
